// Logisim project Circuit.circ as structural Verilog: 1 circuit, main circuit main
// IR
module main (
  input  [3:0] in_1,
  input  [2:0] in_2,
  input  clr,
  input  in_4,
  input  in_5,
  input  in_6,
  input  in_7,
  input  clr_2,
  input  in_9,
  input  in_10,
  input  in_11,
  input  in_12,
  input  in_13,
  input  in_14,
  input  clr_3,
  input  in_16,
  input  in_17
);

  wire clock_1_out, undriven;
  wire [6:0] AR_q, bitselector_1_out, bitselector_2_out, PC_q;
  wire [15:0] AC, adder_1_out, adder_2_out, ALU, and_1_out, bit_extender_1_out, bit_extender_2_out, BUS, DR,
       IR_q, multiplier_1_out, multiplier_2_out, not_1_out, not_2_out, ram_1_data, TR_q;

  Clock clock_1 (.out(clock_1_out));
  BitSelector #(.width(16), .group(7)) bitselector_1 (.in(BUS), .out(bitselector_1_out));  // open: sel
  BitSelector #(.width(16), .group(7)) bitselector_2 (.in(BUS), .out(bitselector_2_out));  // open: sel
  Counter #(.width(7), .max('h7f)) AR (
    .load(in_4), .D(bitselector_1_out), .count(in_5), .Q(AR_q), .clk(clock_1_out), .clr(clr));  // open: carry
  Counter #(.width(7), .max('h7f)) PC (
    .load(in_6), .D(bitselector_2_out), .count(in_12), .Q(PC_q), .clk(clock_1_out), .clr(clr_2));  // open: carry
  Counter #(.width(16), .max('hffff)) u_AC (
    .load(in_7), .D(ALU), .count(in_9), .Q(AC), .clk(clock_1_out), .clr(clr_2));  // open: carry
  Counter #(.width(16), .max('hffff)) u_DR (
    .load(in_10), .D(BUS), .count(in_12), .Q(DR), .clk(clock_1_out), .clr(clr_2));  // open: carry
  Counter #(.width(16), .max('hffff)) TR (
    .load(in_11), .D(BUS), .count(in_12), .Q(TR_q), .clk(clock_1_out), .clr(clr_2));  // open: carry
  Counter #(.width(16), .max('hffff)) IR (
    .load(in_14), .D(BUS), .count(in_12), .Q(IR_q), .clk(clock_1_out), .clr(clr_3));  // open: carry
  assign bit_extender_1_out = {{9{1'b0}}, AR_q};  // Bit_Extender bit_extender_1
  assign bit_extender_2_out = {{9{1'b0}}, PC_q};  // Bit_Extender bit_extender_2
  RAM #(.addrWidth(7), .dataWidth(16), .bus("separate")) ram_1 (
    .addr(AR_q), .din(BUS), .data(ram_1_data), .str(in_13), .sel(undriven), .clk(clock_1_out), .ld(in_17),
    .clr(clr_3));
  Multiplexer #(.select(3), .width(16), .disabled(0), .enable("false")) multiplexer_1 (
    .in1(bit_extender_1_out), .in2(bit_extender_2_out), .in3(AC), .in4(DR), .in5(TR_q), .in6(ram_1_data),
    .in7(IR_q), .out(BUS), .sel(in_2));  // open: in0
  Adder #(.width(16)) adder_1 (.a(AC), .b(DR), .out(adder_1_out));  // open: cin, cout
  Adder #(.width(16)) adder_2 (.a(AC), .b(BUS), .out(adder_2_out));  // open: cin, cout
  Multiplier #(.width(16)) multiplier_1 (.a(DR), .b(AC), .out(multiplier_1_out));  // open: cin, cout
  Multiplier #(.width(16)) multiplier_2 (.a(BUS), .b(AC), .out(multiplier_2_out));  // open: cin, cout
  assign and_1_out = DR & AC;  // AND_Gate and_1, 16 bits wide
  assign not_1_out = ~AC;  // NOT_Gate not_1, 16 bits wide
  assign not_2_out = ~BUS;  // NOT_Gate not_2, 16 bits wide
  Multiplexer #(.select(4), .width(16), .disabled(0), .enable("false")) multiplexer_2 (
    .in1(DR), .in2(BUS), .in3(adder_1_out), .in4(adder_2_out), .in5(and_1_out), .in6(not_1_out),
    .in7(not_2_out), .in8(multiplier_1_out), .in9(multiplier_2_out), .out(ALU), .sel(in_1));  // open: in0, in10, in11, in12, in13, in14, in15
endmodule
